// Logisim project reg_ref_inst.circ as structural Verilog: 1 circuit, main circuit main
module main (
  input  [15:0] in_1,
  input  in_2,
  input  [15:0] in_3,
  input  in_4,
  input  [3:0] in_5,
  input  [15:0] in_6,
  input  [11:0] in_7,
  input  [11:0] in_8,
  input  in_9,
  input  in_10,
  input  [15:0] in_11,
  output out_12,
  output [15:0] out_13,
  output [11:0] out_14
);

  wire and_2_out, and_3_out, and_4_out, comparator_1_eq, multiplexer_3_out, not_1_out, not_2_out, not_3_out,
       or_3_out, or_4_out, or_5_out, xnor_1_out;
  wire [1:0] or_2_out;
  wire [11:0] adder_2_out, multiplexer_4_out;
  wire [15:0] adder_1_out, multiplexer_1_out, multiplexer_2_out, negator_1_out, shifter_1_out, shifter_2_out;
  wire [15:15] E_q;

  and and_1 (out_12, in_1[12], in_1[13], in_1[14], not_1_out);
  not not_1 (not_1_out, in_1[15]);
  or or_1 (or_2_out[1], in_1[6], in_1[5]);
  or or_2 (or_2_out[0], in_1[7], in_1[5]);
  Adder #(.width(16)) adder_1 (.a(out_13), .b(in_6), .out(adder_1_out));  // open: cin, cout
  Comparator #(.width(16)) comparator_1 (.a(out_13), .b(in_11), .eq(comparator_1_eq));  // open: gt, lt
  Negator #(.width(16)) negator_1 (.in(out_13), .out(negator_1_out));
  Shifter #(.width(16), .shift("lr")) shifter_1 (.in(out_13), .\dist (in_5), .out(shifter_1_out));
  Shifter #(.width(16)) shifter_2 (.in(out_13), .\dist (in_5), .out(shifter_2_out));
  xnor xnor_1 (xnor_1_out, E_q[15], in_9);
  not not_2 (not_2_out, out_13[15]);
  Adder #(.width(12)) adder_2 (.a(in_7), .b(out_14), .out(adder_2_out));  // open: cin, cout
  or or_3 (or_3_out, comparator_1_eq, xnor_1_out, out_13[15], not_2_out);
  and and_2 (and_2_out, in_1[11], out_12);
  and and_3 (and_3_out, out_12, in_1[10]);
  or or_4 (or_4_out, in_1[4], in_1[3], in_1[2], in_1[1]);
  or or_5 (or_5_out, in_1[7], in_1[6]);
  Multiplexer #(.select(2), .width(16)) multiplexer_1 (
    .in0(negator_1_out), .in1({E_q[15], shifter_1_out[14:0]}), .in2({shifter_2_out[15:1], E_q[15]}),
    .in3(adder_1_out), .out(multiplexer_1_out), .sel(or_2_out), .en(out_12));
  and and_4 (and_4_out, or_4_out, out_12, or_3_out);
  Multiplexer #(.width(16)) multiplexer_2 (
    .in0(in_3), .in1(multiplexer_1_out), .out(multiplexer_2_out), .sel(in_4));  // open: en
  Multiplexer multiplexer_3 (.in0(out_13[0]), .in1(out_13[15]), .out(multiplexer_3_out), .sel(in_1[6]), .en(or_5_out));
  not not_3 (not_3_out, multiplexer_3_out);
  Register #(.width(16)) AC (.D(multiplexer_2_out), .Q(out_13), .clk(in_2), .clr(and_2_out));  // open: en
  J_K_Flip_Flop E (
    .J(multiplexer_3_out), .clk(in_2), .K(not_3_out), .Q(E_q[15]), .reset(and_3_out));  // open: Qn, preset, en
  Multiplexer #(.width(12)) multiplexer_4 (
    .in0(in_8), .in1(adder_2_out), .out(multiplexer_4_out), .sel(in_10), .en(and_4_out));
  Register #(.width(12)) PC (.D(multiplexer_4_out), .Q(out_14), .clk(in_2));  // open: en, clr
  J_K_Flip_Flop S (.clk(in_2), .reset(in_1[0]));  // open: J, K, Q, Qn, preset, en

  // Notes on the sheet:
  //   I'D7
  //   IR 15-0
  //   23BCE208 PARAM DESAI & 23BTM045 SANCIHTA PATHAK
endmodule
